// Digital circuit Acc8-seq.dig as structural Verilog
module Acc8_seq (
  input  en,
  input  clk,
  input  rst,
  output [7:0] R,
  output OVF
);

  wire [3:0] counter_1_out;
  wire [7:0] rom_1_d;

  Counter #(.Bits(4)) counter_1 (.en(en), .C(clk), .clr(1'b0), .out(counter_1_out), .ovf(OVF));
  ROM #(.AddrBits(4), .Bits(8)) rom_1 (.A(counter_1_out), .sel(1'b1), .D(rom_1_d));
  Acc8s acc8s_1 (.en(en), .rst(rst), .CLK(clk), .A(rom_1_d), .R(R), .OVF(OVF));

  // Notes on the sheet:
  //   contents of rom_1 (hex, n*v repeats v):
  //   1,10,10,11
endmodule
