// Digital circuit Acc8-smem.dig as structural Verilog
module Acc8_smem (
  input  clk,
  input  [7:0] ADDR,
  input  ld,
  input  rst,
  input  en,
  output [7:0] R,
  output OVF
);

  wire and_1_out;
  wire [7:0] counterpreset_1_out, smem_1_data;

  CounterPreset #(.Bits(8)) counterpreset_1 (
    .en(en), .C(clk), .dir(1'b0), .in(ADDR), .ld(ld), .clr(rst), .out(counterpreset_1_out));  // open: ovf
  // Probe on counterpreset_1_out
  smem smem_1 (.ADDR(counterpreset_1_out), .en(en), .DATA(smem_1_data));
  and and_1 (and_1_out, en, ~ld);  // And
  Acc8 acc8_1 (.en(and_1_out), .rst(rst), .CLK(clk), .AS(1'b0), .A(smem_1_data), .R(R), .OVF(OVF));
endmodule
