// Digital circuit Acc8.dig as structural Verilog
module Acc8 (
  input  en,
  input  rst,
  input  CLK,
  input  AS,
  input  [7:0] A,
  output [7:0] R,
  output OVF
);

  wire [7:0] addsub8_ovf_1_r;

  AddSub8_ovf addsub8_ovf_1 (.A(A), .B(R), .AS(AS), .OVF(OVF), .R(addsub8_ovf_1_r));
  // Reg8 reg8_1: pin names not known; wires that end beside it: CLK, addsub8_ovf_1_r, rst, en, R
endmodule
