// Digital circuit Acc8s.dig as structural Verilog
module Acc8s (
  input  en,
  input  rst,
  input  CLK,
  input  [7:0] A,
  output [7:0] R,
  output OVF
);

  wire not_1_out;
  wire [7:0] addsub8_ovf_1_r;

  AddSub8_ovf addsub8_ovf_1 (.A(A), .B(R), .AS(not_1_out), .OVF(OVF), .R(addsub8_ovf_1_r));
  not not_1 (not_1_out, en);
  // Reg8 reg8_1: pin names not known; wires that end beside it: CLK, addsub8_ovf_1_r, rst, en, R
endmodule
