// Digital circuit Add8.dig as structural Verilog
module Add8 (
  input  A0,
  input  B0,
  input  A1,
  input  B1,
  input  A2,
  input  B2,
  input  A3,
  input  B3,
  input  A4,
  input  B4,
  input  A5,
  input  B5,
  input  A6,
  input  B6,
  input  A7,
  input  B7,
  input  AS,
  output S0,
  output S1,
  output S2,
  output S3,
  output S4,
  output S5,
  output S6,
  output S7
);

  wire somador_1_co, somador_2_co, somador_3_co, somador_4_co, somador_5_co, somador_6_co, somador_7_co;

  Somador somador_1 (.A(A0), .B(B0), .Ci(AS), .S(S0), .Co(somador_1_co));
  Somador somador_2 (.A(A1), .B(B1), .Ci(somador_1_co), .S(S1), .Co(somador_2_co));
  Somador somador_3 (.A(A2), .B(B2), .Ci(somador_2_co), .S(S2), .Co(somador_3_co));
  Somador somador_4 (.A(A3), .B(B3), .Ci(somador_3_co), .S(S3), .Co(somador_4_co));
  Somador somador_5 (.A(A4), .B(B4), .Ci(somador_4_co), .S(S4), .Co(somador_5_co));
  Somador somador_6 (.A(A5), .B(B5), .Ci(somador_5_co), .S(S5), .Co(somador_6_co));
  Somador somador_7 (.A(A6), .B(B6), .Ci(somador_6_co), .S(S6), .Co(somador_7_co));
  Somador somador_8 (.A(A7), .B(B7), .Ci(somador_7_co), .S(S7));  // open: Co
endmodule
