// Digital circuit AddSub8-ovf.dig as structural Verilog
module AddSub8_ovf (
  input  [7:0] A,
  input  [7:0] B,
  input  AS,
  output OVF,
  output [7:0] R
);

  AddSub8 addsub8_1 (.A(A), .B(B), .AS(AS), .S(R));
  det_0VF det_0vf_1 (.AS(AS), .sA(A[7]), .sB(B[7]), .sR(R[7]), .OVF(OVF));
endmodule
