// Digital circuit Somador.dig as structural Verilog
module Somador (
  input  A,
  input  B,
  input  Ci,
  output S,
  output Co
);

  wire and_1_out, and_2_out, and_3_out, and_4_out, and_5_out, and_6_out, and_7_out, not_1_out, not_2_out,
       not_3_out;

  not not_1 (not_1_out, A);
  not not_2 (not_2_out, B);
  not not_3 (not_3_out, Ci);
  and and_1 (and_1_out, not_1_out, not_2_out, Ci);
  and and_2 (and_2_out, not_1_out, B, not_3_out);
  and and_3 (and_3_out, A, not_2_out, not_3_out);
  and and_4 (and_4_out, A, B, Ci);
  and and_5 (and_5_out, A, Ci);
  and and_6 (and_6_out, A, B);
  and and_7 (and_7_out, B, Ci);
  or or_1 (S, and_1_out, and_2_out, and_3_out, and_4_out);
  or or_2 (Co, and_5_out, and_6_out, and_7_out);
endmodule
