// Digital circuit dec2-4.dig as structural Verilog
module dec2_4 (
  input  [1:0] s,
  input  en,
  output o0,
  output o1,
  output o2,
  output o3
);

  wire decoder_1_out_0, decoder_1_out_1, decoder_1_out_2, decoder_1_out_3;

  Decoder #(.Selector_Bits(2)) decoder_1 (
    .sel(s), .out_0(decoder_1_out_0), .out_1(decoder_1_out_1), .out_2(decoder_1_out_2),
    .out_3(decoder_1_out_3));
  and and_1 (o0, decoder_1_out_0, en);
  and and_2 (o1, decoder_1_out_1, en);
  and and_3 (o2, decoder_1_out_2, en);
  and and_4 (o3, decoder_1_out_3, en);

  // Notes on the sheet:
  //   Descodificador de 2 para 4 com enable
endmodule
